# Fritzing sketch allohomora (saved by Fritzing 0.9.3b)
breadboards: 1

parts:
  Ring = Pushbutton [package="[THT]"]
  Open = Pushbutton [package="[THT]"]
  KY-1 = Keyes Relay [package=THT]
  Raspberry_Pi_1 = Raspberry Pi B rev2

nets:
  N1: Ring.Pin_1, Ring.Pin_2, Ring.Pin_3, Ring.Pin_4, Open.Pin_1, Open.Pin_2, Open.Pin_3, Open.Pin_4, KY-1.ground, Raspberry_Pi_1.GND, Raspberry_Pi_1.GPIO_18, Raspberry_Pi_1.GPIO_4
  N2: KY-1.signal, Raspberry_Pi_1.GPIO_17
  N3: KY-1.power, Raspberry_Pi_1.5V

custom parts:
  Keyes Relay: The Keyes 5V relay module is suitable for SCM development, home appliance control. It uses a 5V~12V TIL control signal which can control DC / AC signal.
